# Fritzing sketch Alarma _2 (saved by Fritzing 0.9.3b)
breadboards: 1

parts:
  Componente1 = Arduino Uno (Rev3)
  TTP223B1 = TTP223B Capacitive Touch Sensor Module
  Part1 = KY-008 Laser Transmitter Module [package="Breakout board"]
  Part2 = KY-012 Active Buzzer Module [package="Breakout board"]
  R1 = Resistor [tolerance=±5% resistance=10k package=THT]
  R2 = PHOTOCELL [package=photocell]

nets:
  N1: Componente1.A1, R1.Pin_1, R2.P$1
  N2: Componente1.D2, TTP223B1.SIG
  5V: Componente1.5V, TTP223B1.VCC, Part1.S, Part2.S, R1.Pin_0
  GND: Componente1.GND, TTP223B1.GND, Part1.-, Part2.-, R2.P$2

custom parts:
  TTP223B Capacitive Touch Sensor Module: The TTP223B capacitive touch sensor module uses the TTP223B IC. The appropriate voltage is approximately 2 to 5.5 volts.
  KY-008 Laser Transmitter Module: Laser Transmitter module KY-008 for Arduino, emits a dot shaped red laser beam.
  KY-012 Active Buzzer Module: Active Piezoelectric Buzzer Module Keyes KY-012, it produces single-tone sound when signal is high.
