# Fritzing sketch prueba RGB (saved by Fritzing 0.9.3b)
breadboards: 1

parts:
  Componente1 = Arduino Uno (Rev3)
  Componente2 = Bluetooth HC-05 Macho
  Componente3 = HY-SRF05 Ultrasonic Rangefinder
  8_Channel_Relay1 = 8 Channel Power Relay
  Power_plug1 = Power plug
  LED3 = smd LED [color="White (4500K)" package="1206 [SMD]"]
  LED1 = RGB LED (com. cathode, rbg) [package="5 mm [THT]"]
  Power_plug2 = Power plug
  Power_plug4 = Power plug

nets:
  N1: Componente1.D9_PWM, Componente3.Echo
  N2: Componente1.D10_PWM/SS, Componente3.Trig
  N3: Componente1.D2, Componente2.TXD
  N4: Componente1.D3_PWM, Componente2.RXD
  N5: Componente1.D4, 8_Channel_Relay1.IN4
  N6: Componente1.D5_PWM, 8_Channel_Relay1.IN1
  N7: Componente1.D6_PWM, 8_Channel_Relay1.IN2
  N8: Componente1.D7, 8_Channel_Relay1.IN3
  GND: Componente1.GND, Componente2.GND, Componente3.GND, Power_plug4.GND
  VCC: Componente2.VCC, Componente3.Vcc, Power_plug4.VCC
  N9: 8_Channel_Relay1.NC#21, LED1.red_anode
  N10: 8_Channel_Relay1.COM#22, 8_Channel_Relay1.COM#25, 8_Channel_Relay1.COM#28, Power_plug2.GND
  N11: 8_Channel_Relay1.NC#24, LED1.green_anode
  N12: 8_Channel_Relay1.NC#27, LED1.blue_anode
  N13: 8_Channel_Relay1.NC#30, LED3.anode
  N14: 8_Channel_Relay1.COM#31, Power_plug1.VCC
  N15: Power_plug1.GND, LED3.cathode
  N16: LED1.common_cathode, Power_plug2.VCC

custom parts:
  8 Channel Power Relay: An 8 channel power relay. The module operates at 5V.
