# Fritzing sketch Touch y laser (saved by Fritzing 0.9.3b)
breadboards: 1

parts:
  Componente1 = Arduino Uno (Rev3)
  R1 = Photocell (LDR) [package=THT]
  R2 = Resistor [tolerance=±5% resistance=10k package=THT]
  TTP223B1 = TTP223B Capacitive Touch Sensor Module
  Part1 = KY-008 Laser Transmitter Module [package="Breakout board"]

nets:
  N1: Componente1.A1, R1.pin_1, R2.Pin_1
  N2: Componente1.D2, TTP223B1.SIG
  N3: Componente1.D3_PWM, Part1.S
  5V: Componente1.5V, R2.Pin_0, TTP223B1.VCC
  GND: Componente1.GND, R1.pin_0, TTP223B1.GND, Part1.-

custom parts:
  TTP223B Capacitive Touch Sensor Module: The TTP223B capacitive touch sensor module uses the TTP223B IC. The appropriate voltage is approximately 2 to 5.5 volts.
  KY-008 Laser Transmitter Module: Laser Transmitter module KY-008 for Arduino, emits a dot shaped red laser beam.
